# Fritzing sketch sketch-baiov2 (saved by Fritzing 0.9.4)
circuit board: 14.4362cm x 10.0011cm
breadboards: 1

parts:
  Core = NodeMCU V3.0
  J1 = Screw terminal - 2 pins [package=THT]
  Reg = Voltage Regulator - 5V [package="DPak [SMD]"]
  C1_-_0_22uF = Capacitor [package=cap-pth-small]
  C2_-_0_1uF = Capacitor [package=cap-pth-small]
  MuX16_1 = Analog Digital MUX Breakout
  CSM = DFRobot Capacitive Soil Moisture Sensor V1.0 [part_number=SEN0193]
  R1 = Photocell (LDR) [package=THT]
  R2 = Resistor [tolerance=±5% resistance=10k package=THT]
  Water_Level_Sensor1 = Water Level Sensor
  Relay = KY-019 5V Relay Module [package="Breakout board"]
  U4 = TRANSISTOR_NPN_2 [package=to-92]
  U1 = TRANSISTOR_NPN_2 [package=to-92]
  U2 = TRANSISTOR_NPN_2 [package=to-92]
  U5 = TRANSISTOR_NPN_2 [package=to-92]
  U6 = Vibration Motor- ROB-08449 [package=vibe-motor-10mm]
  Componente1 = Lilypad Battery Connect
  U7 = SWITCH-SPST-2 [package=r_sw_th]
  LED1 = LED - 3mm [color="Red (633nm)" package="3 mm [THT]"]
  R3 = Resistor [tolerance=±5% resistance=100 package=THT]

nets:
  N1: Core.D0, Core.RST
  N2: Core.D1, MuX16_1.S0
  N3: Core.D2, MuX16_1.S1
  N4: Core.D3, U1.B
  N5: Core.D4, U2.B
  GND: Core.GND, J1.pin1, Reg.GND, C1_-_0_22uF.2, C2_-_0_1uF.2, R2.Pin_1, U4.C, U1.C, U2.C, U5.C, U6.+, Componente1.-, LED1.cathode
  N6: Core.D5, U5.B
  N7: Core.D6, Relay.S
  N8: Core.D7, U4.B
  N9: Core.D8, R3.Pin_1
  VCC: Core.Vin, Reg.output_voltage, C2_-_0_1uF.1, MuX16_1.VCC, CSM.VCC, R1.pin_0, Water_Level_Sensor1.VCC, Relay.+, Relay.Common
  N10: Core.A0, MuX16_1.SIG
  N11: J1.pin2, Reg.input_voltage, C1_-_0_22uF.1, U7.O
  N12: MuX16_1.C0, CSM.A
  N13: MuX16_1.C1, R1.pin_1, R2.Pin_0
  N14: MuX16_1.C2, Water_Level_Sensor1.SIG
  N15: MuX16_1.GND, U1.E
  N16: CSM.GND, U2.E
  N17: Water_Level_Sensor1.GND, U5.E
  N18: Relay.-, U4.E
  N19: Relay.NO, U6.-
  N20: Componente1.+, U7.P
  N21: LED1.anode, R3.Pin_0

custom parts:
  NodeMCU V3.0: NodeMcu V3 Lua WIFI Development Board
  DFRobot Capacitive Soil Moisture Sensor V1.0: DFRobot Capacitive Soil Moisture Sensor V1.0 This product measures soil moisture levels by capacitive sensing, rather than resistive sensing like other types of moisture sensor. It is made of a corrosion resistant material giving it a long service life. Insert it into soil and impress your friends with the real-time soil moisture data! The product includes an on-board voltage regulator which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
  Water Level Sensor: A water level sensor. This sensor operates at 3V to 5V. The Sig (signal) pin outputs an analogue signal that is in proportion to the amount of water in contact with the sensor.
  KY-019 5V Relay Module: KY-019 5V Relay module, used to control AC circuits.
